# Fritzing sketch Core (saved by Fritzing 0.9.3b)
circuit board: 6.88807cm x 4.93695cm
breadboards: 1

parts:
  J2 = female pin header, 14 pins [form="♀ (female)"]
  J1 = female pin header, 14 pins [form="♀ (female)"]
  J3 = female pin header, 4 pins [form="♀ (female)"]
  J4 = female pin header, 4 pins [form="♀ (female)"]
  J5 = female pin header, 4 pins [form="♀ (female)"]
  J6 = female pin header, 4 pins [form="♀ (female)"]
  J7 = female pin header, 4 pins [form="♀ (female)"]
  J8 = female pin header, 4 pins [form="♀ (female)"]
  J9 = female pin header, 4 pins [form="♀ (female)"]
  J10 = female pin header, 4 pins [form="♀ (female)"]
  J11 = female pin header, 4 pins [form="♀ (female)"]
  LED1 = RGB LED - (4 legs) [package="5 mm [THT]"]  # not connected
  X1 = USB Connectors [package=usb-b-pth]
  J12 = female pin header, 2 pins [form="♀ (female)"]
  J13 = female pin header, 2 pins [form="♀ (female)"]
  U1 = microSD Socket [package="Molex 502774-0891 [SMD]"]  # not connected
  J16 = Power Jack [package=power_jack_slot]
  C10 = Electrolytic Capacitor [capacitance=10µF rated_voltage=35V package="100 mil [THT, electrolytic]"]
  C11 = Electrolytic Capacitor [capacitance=10µF rated_voltage=35V package="100 mil [THT, electrolytic]"]
  U4 = Voltage Regulator - 5V [package="TO220 [THT]"]
  R1 = Resistor [tolerance=±5% resistance=220 package=THT]
  R2 = Resistor [tolerance=±5% resistance=220 package=THT]
  R3 = Resistor [tolerance=±5% resistance=220 package=THT]
  R4 = Resistor [tolerance=±5% resistance=220 package=THT]
  R5 = Resistor [tolerance=±5% resistance=220 package=THT]

nets:
  GND: J2.pin14, J3.pin4, J4.pin4, J5.pin4, J9.pin1, J10.pin1, J11.pin1, X1.GND, J16.GNDBREAK, J16.GND, C10.-, C11.-, U4.GND
  N1: J1.pin6, R1.Pin_1
  N2: J1.pin7, R2.Pin_1
  N3: J1.pin8, R3.Pin_1
  N4: J1.pin9, R4.Pin_1
  N5: J1.pin10, R5.Pin_1
  N6: J1.pin14, J3.pin1, J4.pin1, J5.pin1, J12.pin1, C11.+, U4.output_voltage
  N7: J3.pin2, J4.pin2, J5.pin2
  N8: J3.pin3, J4.pin3, J5.pin3
  N9: J6.pin1, J7.pin1, J8.pin1, J9.pin2, J9.pin3, J10.pin2, J10.pin3, J11.pin2, J11.pin3, R1.Pin_0, R2.Pin_0
  N10: J6.pin2, J7.pin2, J8.pin2
  N11: J6.pin3, J7.pin3, J8.pin3
  N12: J6.pin4, J7.pin4, J8.pin4
  N13: J9.pin4, J10.pin4, J11.pin4
  N14: X1.D+, J13.pin1
  N15: X1.D-, J13.pin2
  N16: X1.VBUS, J12.pin2
  N17: J16.PWR, C10.+, U4.input_voltage
